# Fritzing sketch DDPKey (saved by Fritzing 0.9.3b)
breadboards: 1

parts:
  Part1 = Arduino Uno (Rev3) [part_number=3]
  U1 = GAS_SENSOR [package=mq-3]
  U2 = ADMP504 - Ultralow Noise Microphone with Bottom Port and Analog Output [part_number=ADMP504]
  VCC1 = 4 x AAA Battery Mount
  VCC2 = 4 x AAA Battery Mount
  LED1 = LED - 5mm [color="Red (633nm)" package="5 mm [THT]"]
  LED2 = LED - 5mm [color="Yellow (595nm)" package="5 mm [THT]"]
  R1 = Resistor [tolerance=±5% resistance=220 package=THT]
  R2 = Resistor [tolerance=±5% resistance=220 package=THT]
  Q1 = NPN-Transistor [package="TO92 [THT]"]
  D1 = Diode [package=diode-1n4001]
  U3 = RELAY [package=relay-t9a]
  S1 = SWITCH-MOMENTARY-2 [package=tactile-pth-12mm]
  L1 = Solenoid

nets:
  N1: Part1.A0, U2.GND
  N2: Part1.A1, U1.A1
  N3: Part1.D9_PWM, Q1.B
  N4: Part1.D10_PWM/SS, LED2.anode
  N5: Part1.D13/SCK, LED1.anode
  N6: Part1.GND, R1.Pin_0, R2.Pin_0, S1.2
  N7: Part1.VIN, VCC1.+
  N8: U1.B1, U1.H1, U2.OUTPUT, VCC1.-, VCC2.-, U3.NC, S1.1, L1.pin1
  N9: U1.H2, U2.NC, VCC2.+, Q1.C, U3.NO
  N10: LED1.cathode, R2.Pin_1
  N11: LED2.cathode, R1.Pin_1
  N12: Q1.E, D1.C, U3.COIL1
  N13: D1.A, U3.COIL2
  N14: U3.MAIN, L1.pin2
